// Logisim project LC-2200-16.circ as structural Verilog: 3 circuits, main circuit Alu
module main (
  input  in_1,
  input  in_2,
  input  in_3,
  input  in_4,
  input  in_5,
  input  in_6,
  input  in_7,
  input  in_8,
  input  in_9,
  input  in_10,
  input  in_11,
  input  in_12,
  input  in_13,
  input  in_14,
  input  in_15,
  input  in_16,
  input  in_17,
  output [15:0] out_18,
  output [2:0] OP,
  output [3:0] regno,
  output out_21
);

  wire Clk, Clr, comparator_1_eq, comparator_2_eq, mem;
  wire [12:0] IR;
  wire [15:0] A_q, Alu_output, B_q, bit_extender_1_out, MAR_q, multiplexer_1_out, PC_q, ram_1_data,
       ram_2_data;

  Clock clock_1 (.out(Clk));
  Button button_1 (.out(Clr));
  Button button_2 (.out(mem));
  Register #(.width(16)) PC (.D(out_18), .en(in_2), .Q(PC_q), .clk(Clk), .clr(Clr));
  assign out_18 = in_7 ? PC_q : 16'bz;  // Controlled_Buffer controlled_buffer_1
  Register #(.width(16)) A (.D(out_18), .en(in_8), .Q(A_q), .clk(Clk));  // open: clr
  Alu Alu (.A(A_q), .B(B_q), .Func({in_17, in_16}), .Output(Alu_output));
  assign out_18 = in_5 ? Alu_output : 16'bz;  // Controlled_Buffer controlled_buffer_2
  Register #(.width(16)) B (.D(out_18), .en(in_10), .Q(B_q), .clk(Clk));  // open: clr
  Comparator #(.width(16)) comparator_1 (.a(out_18), .b({16{1'b0}}), .eq(comparator_1_eq));  // open: gt, lt
  Register #(.width(1)) Z (.D(comparator_1_eq), .en(in_11), .Q(out_21), .clk(Clk));  // open: clr
  Comparator #(.width(4)) comparator_2 (.a(regno), .b(4'b0000), .eq(comparator_2_eq));  // open: gt, lt
  Multiplexer #(.width(16), .enable("false")) multiplexer_1 (
    .in0(ram_1_data), .in1({16{1'b0}}), .out(multiplexer_1_out), .sel(comparator_2_eq));
  RAM #(.addrWidth(4), .dataWidth(16), .bus("separate")) ram_1 (
    .addr(regno), .din(out_18), .data(ram_1_data), .str(in_12), .clk(Clk), .clr(Clr));  // open: sel, ld
  assign out_18 = in_1 ? multiplexer_1_out : 16'bz;  // Controlled_Buffer controlled_buffer_3
  Register #(.width(16)) MAR (.D(out_18), .en(in_6), .Q(MAR_q), .clk(Clk));  // open: clr
  RAM #(.addrWidth(16), .dataWidth(16), .bus("separate")) ram_2 (
    .addr(MAR_q), .din(out_18), .data(ram_2_data), .str(in_13), .clk(Clk), .clr(mem));  // open: sel, ld
  assign out_18 = in_3 ? ram_2_data : 16'bz;  // Controlled_Buffer controlled_buffer_4
  Multiplexer #(.select(2), .width(4), .disabled(0), .enable("false")) multiplexer_2 (
    .in0(IR[12:9]), .in1(IR[8:5]), .in2(IR[4:1]), .out(regno), .sel({in_15, in_14}));  // open: in3
  Register #(.width(16)) u_IR (.D(out_18), .en(in_4), .Q({OP, IR}), .clk(Clk));  // open: clr
  assign out_18 = in_9 ? bit_extender_1_out : 16'bz;  // Controlled_Buffer controlled_buffer_5
  assign bit_extender_1_out = {{11{1'b0}}, IR[4:0]};  // Bit_Extender bit_extender_1

  // Other names for the same wires on the sheet: DrALU = in_5; DrMEM = in_3; DrOFF = in_9; DrPC = in_7; DrREG = in_1;
  //   ALULo = in_16; Func[1:0] = {in_17, in_16}; ALUHi = in_17; RY[3:0] = IR[8:5]; RX[3:0] = IR[12:9]; IR[15:13] = OP;
  //   LdA = in_8; LdB = in_10; LdIR = in_4; LdMAR = in_6; LdPC = in_2; LdZ = in_11; offset[4:0] = IR[4:0];
  //   RZ[3:0] = IR[4:1]; Reg_Sel[1:0] = {in_15, in_14}; RegSelLo = in_14; RegSelHi = in_15; WrMEM = in_13;
  //   WrREG = in_12; Z = out_21
endmodule

module Alu (
  input  [15:0] A,
  input  [15:0] B,
  input  [1:0] Func,
  output [15:0] Output
);

  wire [15:0] adder_1_out, adder_2_out, nand_1_out, subtractor_1_out;

  Adder #(.width(16)) adder_1 (.a(A), .b(B), .out(adder_1_out));  // open: cin, cout
  assign nand_1_out = ~(A & B);  // NAND_Gate nand_1, 16 bits wide
  Subtractor #(.width(16)) subtractor_1 (.a(A), .b(B), .out(subtractor_1_out));  // open: bin, bout
  Adder #(.width(16)) adder_2 (.a(A), .b(16'h1), .out(adder_2_out));  // open: cin, cout
  Multiplexer #(.select(2), .width(16), .enable("false")) multiplexer_1 (
    .in0(adder_1_out), .in1(nand_1_out), .in2(subtractor_1_out), .in3(adder_2_out), .out(Output), .sel(Func));
endmodule

module Microcontroller (
  output [2:0] opcode,
  output [15:0] value_on_bus,
  output [3:0] out_3
);

  wire button_1_out, Clk;
  wire [0:0] datapath_out_21;
  wire [5:0] multiplexer_1_out, Nextstage, rom_2_data, rom_3_data, State_register_q;
  wire [24:6] rom_1_data;

  ROM #(.addrWidth(6), .dataWidth(25)) rom_1 (.addr(State_register_q), .data({rom_1_data, Nextstage}));  // open: sel
  Register #(.width(6)) State_register (
    .D(multiplexer_1_out), .Q(State_register_q), .clk(Clk), .clr(button_1_out));  // open: en
  Button button_1 (.out(button_1_out));
  Clock clock_1 (.out(Clk));
  main datapath (
    .in_1(rom_1_data[6]), .in_3(rom_1_data[7]), .in_5(rom_1_data[8]), .in_7(rom_1_data[9]),
    .in_9(rom_1_data[10]), .in_2(rom_1_data[11]), .in_4(rom_1_data[12]), .in_6(rom_1_data[13]),
    .in_8(rom_1_data[14]), .in_10(rom_1_data[15]), .in_11(rom_1_data[16]), .OP(opcode),
    .out_21(datapath_out_21[0]), .in_12(rom_1_data[17]), .out_18(value_on_bus), .in_13(rom_1_data[18]),
    .in_16(rom_1_data[21]), .in_17(rom_1_data[22]), .in_14(rom_1_data[19]), .in_15(rom_1_data[20]),
    .regno(out_3));
  Multiplexer #(.select(2), .width(6), .enable("false")) multiplexer_1 (
    .in0(Nextstage), .in1(rom_2_data), .in2(rom_3_data), .out(multiplexer_1_out), .sel(rom_1_data[24:23]));  // open: in3
  ROM #(.addrWidth(3), .dataWidth(6)) rom_2 (.addr(opcode), .data(rom_2_data));  // open: sel
  ROM #(.addrWidth(2), .dataWidth(6)) rom_3 (.addr({1'b0, datapath_out_21[0]}), .data(rom_3_data));  // open: sel

  // Notes on the sheet:
  //   contents of rom_1 (hex, n*v repeats v):
  //   6201 1082 e00900 84044 108045 20100 84047 108048 220100 8404a 840b 20100 8404d 840e 210f 20080 84051
  //   8412 2113 40040 4055 88056 1410100 6202 4219 841a 900 a021c 840 1d
  //   contents of rom_2 (hex, n*v repeats v):
  //   3 6 9 c 10 14 1b 1d
  //   contents of rom_3 (hex, n*v repeats v):
  //   17 18
endmodule
