// Logisim project LC-2200-32.circ as structural Verilog: 6 circuits, main circuit Processor
module Processor (
  output [31:0] out_1,
  output [10:0] out_2,
  output [31:0] out_3,
  output out_4,
  output [31:0] out_5
);

  wire and_1_out, and_2_out, and_3_out, and_6_out, and_7_out, and_8_out, button_2_out, ch, Clock, Clr,
       comparator_1_eq, comparator_1_gt, dis, DrALU, DrEnInt, DrMEM, DrOFF, DrPC, DrReg, have, IE, Int,
       Intsignal, keyboard_1_avail, LdA, LdB, LdEnInt, LdIR, LdMAR, LdPC, LdZ, not_1_out, not_2_out,
       not_3_out, not_4_out, or_1_out, or_2_out, or_3_out, or_4_out, WrMEM, WrREG, Z, ZeroDetectOut;
  wire [1:0] FUNC, RegSel;
  wire [3:0] Reg_num;
  wire [23:0] MAR_q;
  wire [31:0] A_q, B_q, multiplexer_1_out, PC_q, ram_1_data, registers_1_data_out, ZeroDetect;

  or or_1 (or_1_out, comparator_1_eq, comparator_1_gt);
  and and_1 (and_1_out, FUNC[0], FUNC[1], LdZ);
  Clock clock_1 (.out(Clock));
  Register #(.width(32)) PC (.D(out_3), .en(LdPC), .Q(PC_q), .clk(Clock), .clr(Clr));
  Comparator #(.width(32)) comparator_1 (.a(PC_q), .b(32'h10), .gt(comparator_1_gt), .eq(comparator_1_eq));  // open: lt
  Multiplexer #(.width(32), .enable("false")) multiplexer_1 (
    .in0(32'h10), .in1(PC_q), .out(multiplexer_1_out), .sel(or_1_out));
  assign out_3 = DrPC ? multiplexer_1_out : 32'bz;  // Controlled_Buffer controlled_buffer_1
  and and_2 (and_2_out, IE, or_2_out);
  or or_2 (or_2_out, have, Int);
  Keyboard keyboard_1 (.clk(and_1_out), .re(1'b1), .clr(Clr), .avail(keyboard_1_avail), .data(out_5[6:0]));
  Register #(.width(1)) Z_Register (.D(ZeroDetectOut), .en(LdZ), .Q(Z), .clk(Clock), .clr(Clr));
  State_Machine state_machine_1 (
    .Clock(Clock), .cir(Clr), .OpCode(out_1[31:28]), .Z(Z), .Int(and_2_out), .DrREG(DrReg), .DrMEM(DrMEM),
    .DrALU(DrALU), .DrPC(DrPC), .DrOFF(DrOFF), .LdPC(LdPC), .LdIR(LdIR), .LdMAR(LdMAR), .LdA(LdA), .LdB(LdB),
    .LdZ(LdZ), .WrREG(WrREG), .WrMEM(WrMEM), .RegSel(RegSel), .ALU_FUNC(FUNC), .LdEnInt(LdEnInt),
    .DrEnInt(DrEnInt), .IntAck(out_4));  // open: out_24, out_25
  not not_1 (not_1_out, ch);
  and and_3 (and_3_out, keyboard_1_avail, not_1_out);
  Register #(.width(32)) A (.D(out_3), .en(LdA), .Q(A_q), .clk(Clock), .clr(Clr));
  ALU alu_1 (.FUNC(FUNC), .INPUT_A(A_q), .INPUT_B(B_q), .out_4(ZeroDetect));
  and and_4 (have, and_3_out, IE);
  and and_5 (dis, RegSel[0], RegSel[1], DrReg, LdPC);
  Register #(.width(32)) B (.D(out_3), .en(LdB), .Q(B_q), .clk(Clock), .clr(Clr));
  assign out_3 = DrALU ? ZeroDetect : 32'bz;  // Controlled_Buffer controlled_buffer_2
  assign out_3 = and_6_out ? {{25{1'b0}}, out_5[6:0]} : 32'bz;  // Controlled_Buffer controlled_buffer_3
  and and_6 (and_6_out, FUNC[0], FUNC[1], LdZ);
  Button button_1 (.out(Clr));
  Register #(.width(1)) register_1 (.D(DrEnInt), .en(LdEnInt), .Q(IE), .clk(Clock), .clr(Clr));
  Registers registers_1 (
    .WrReg(WrREG), .RegSel(Reg_num), .Data_In(out_3), .Clock(Clock), .ClearRegFile(Clr),
    .Data_Out(registers_1_data_out));
  assign out_3 = DrReg ? registers_1_data_out : 32'bz;  // Controlled_Buffer controlled_buffer_4
  Register #(.width(1)) register_2 (.D(Int), .en(1'b1), .Q(ch), .clk(Int), .clr(or_3_out));
  Button button_2 (.out(button_2_out));
  Intergenerator intergenerator_1 (.out_2(out_2), .IntOut(Intsignal), .CLK(Clock));
  Register #(.width(24)) MAR (.D(out_3[23:0]), .en(LdMAR), .Q(MAR_q), .clk(Clock), .clr(Clr));
  not not_2 (not_2_out, WrMEM);
  Register #(.width(1)) register_3 (.D(Intsignal), .en(1'b1), .Q(Int), .clk(Intsignal), .clr(or_4_out));
  RAM #(.addrWidth(24), .dataWidth(32), .bus("separate")) ram_1 (
    .addr(MAR_q), .din(out_3), .data(ram_1_data), .str(WrMEM), .clk(Clock), .ld(not_2_out), .clr(button_2_out));  // open: sel
  assign out_3 = DrMEM ? ram_1_data : 32'bz;  // Controlled_Buffer controlled_buffer_5
  or or_3 (or_3_out, dis, Clr);
  Register #(.width(32)) IR (.D(out_3), .en(LdIR), .Q(out_1), .clk(Clock), .clr(Clr));
  Multiplexer #(.select(2), .width(4), .enable("false")) multiplexer_2 (
    .in0(out_1[27:24]), .in1(out_1[23:20]), .in2(out_1[3:0]), .in3(4'b1100), .out(Reg_num), .sel(RegSel));
  assign out_3 = DrOFF ? {{13{out_1[19]}}, out_1[18:0]} : 32'bz;  // Controlled_Buffer controlled_buffer_6
  Comparator #(.width(32), .mode("unsigned")) comparator_2 (
    .a(ZeroDetect), .b({32{1'b0}}), .eq(ZeroDetectOut));  // open: gt, lt
  or or_4 (or_4_out, Clr, and_7_out);
  not not_3 (not_3_out, and_8_out);
  and and_7 (and_7_out, out_4, not_3_out);
  assign out_3 = and_7_out ? 32'h1 : 32'bz;  // Controlled_Buffer controlled_buffer_7
  and and_8 (and_8_out, out_4, not_4_out);
  not not_4 (not_4_out, ch);
  assign out_3 = and_8_out ? 32'h3 : 32'bz;  // Controlled_Buffer controlled_buffer_8

  assign out_5[31:7] = {25{1'b0}};

  // Other names for the same wires on the sheet: IntAck = out_4; Opcode[3:0] = out_1[31:28]

  // Notes on the sheet:
  //   00 = RX
  //   01 = RY
  //   10 = RZ
endmodule

module ALU (
  input  [31:0] INPUT_A,
  input  [31:0] INPUT_B,
  input  [1:0] FUNC,
  output [31:0] out_4
);

  wire [31:0] adder_1_out, adder_2_out, nand_1_out, subtractor_1_out;

  Adder #(.width(32)) adder_1 (.a(INPUT_A), .b(INPUT_B), .out(adder_1_out));  // open: cin, cout
  assign nand_1_out = ~(INPUT_A & INPUT_B);  // NAND_Gate nand_1, 32 bits wide
  Multiplexer #(.select(2), .width(32), .enable("false")) multiplexer_1 (
    .in0(adder_1_out), .in1(nand_1_out), .in2(subtractor_1_out), .in3(adder_2_out), .out(out_4), .sel(FUNC));
  Subtractor #(.width(32)) subtractor_1 (.a(INPUT_A), .b(INPUT_B), .out(subtractor_1_out));  // open: bin, bout
  Adder #(.width(32)) adder_2 (.a(INPUT_A), .b(32'h1), .out(adder_2_out));  // open: cin, cout
endmodule

module State_Machine (
  input  Clock,
  input  cir,
  input  [3:0] OpCode,
  input  Z,
  input  Int,
  output DrREG,
  output DrMEM,
  output DrALU,
  output DrPC,
  output DrOFF,
  output LdPC,
  output LdIR,
  output LdMAR,
  output LdA,
  output LdB,
  output LdZ,
  output WrREG,
  output WrMEM,
  output [1:0] RegSel,
  output [1:0] ALU_FUNC,
  output LdEnInt,
  output DrEnInt,
  output IntAck,
  output out_24,
  output out_25
);

  wire chkZ, OpTest;
  wire [5:0] multiplexer_1_out, register_1_q, rom_1_data, rom_2_data, rom_3_data, rom_4_data;

  Register #(.width(6)) register_1 (.D(multiplexer_1_out), .en(Clock), .Q(register_1_q), .clk(Clock), .clr(cir));
  Multiplexer #(.select(2), .width(6), .enable("false")) multiplexer_1 (
    .in0(rom_1_data), .in1(rom_2_data), .in2(rom_4_data), .in3(rom_3_data), .out(multiplexer_1_out),
    .sel({chkZ, OpTest}));
  ROM #(.addrWidth(6), .dataWidth(30)) rom_1 (
    .addr(register_1_q),
    .data({out_25, out_24, IntAck, DrEnInt, LdEnInt, chkZ, OpTest, ALU_FUNC, RegSel, WrMEM, WrREG, LdZ, LdB, LdA, LdMAR, LdIR, LdPC, DrOFF, DrPC, DrALU, DrMEM, DrREG, rom_1_data}));  // open: sel
  ROM #(.addrWidth(4), .dataWidth(6)) rom_2 (.addr(OpCode), .data(rom_2_data));  // open: sel
  ROM #(.addrWidth(2), .dataWidth(6)) rom_3 (.addr({1'b0, Int}), .data(rom_3_data));  // open: sel
  ROM #(.addrWidth(2), .dataWidth(6)) rom_4 (.addr({1'b0, Z}), .data(rom_4_data));  // open: sel

  // Notes on the sheet:
  //   contents of rom_1 (hex, n*v repeats v):
  //   1800000 21a0202 8002003 884 6205 1086 e00900 84048 108049 20100 8404b 10804c 220100 8404e 840f 20100
  //   84051 8412 2113 20080 84055 8416 2117 40040 4059 8805a 41011b 1000000 421d 841e 900 a0220 840 21
  //   6000000 2000000 180862 84066 8427 2128 650000
  //   contents of rom_2 (hex, n*v repeats v):
  //   7 a d 10 14 18 1f 21 29 2b 22 23 24 25 2a
  //   contents of rom_3 (hex, n*v repeats v):
  //   4 1
  //   contents of rom_4 (hex, n*v repeats v):
  //   0 1c
endmodule

// 0?
module Zero_Detection (
  input  [31:0] In,
  output Out
);

  Comparator #(.width(32), .mode("unsigned")) comparator_1 (.a(In), .b({32{1'b0}}), .eq(Out));  // open: gt, lt
endmodule

// Reg File
module Registers (
  input  [31:0] Data_In,
  input  WrReg,
  input  [3:0] RegSel,
  input  Clock,
  input  ClearRegFile,
  output [31:0] Data_Out
);

  wire and_1_out, and_2_out, and_3_out, and_4_out, and_5_out, and_6_out, and_7_out, and_8_out, and_9_out,
       and_10_out, and_11_out, and_12_out, and_13_out, and_14_out, and_15_out, and_16_out, decoder_1_out0,
       decoder_1_out1, decoder_1_out2, decoder_1_out3, decoder_1_out4, decoder_1_out5, decoder_1_out6,
       decoder_1_out7, decoder_1_out8, decoder_1_out9, decoder_1_out10, decoder_1_out11, decoder_1_out12,
       decoder_1_out13, decoder_1_out14, decoder_1_out15;
  wire [31:0] a0, a1, a2, at, k0, pr, ra, s0, s1, s2, sp, t0, t1, t2, v0, zero;

  Decoder #(.select(4), .enable("false")) decoder_1 (
    .out0(decoder_1_out0), .out1(decoder_1_out1), .out2(decoder_1_out2), .out3(decoder_1_out3),
    .out4(decoder_1_out4), .out5(decoder_1_out5), .out6(decoder_1_out6), .out7(decoder_1_out7),
    .out8(decoder_1_out8), .out9(decoder_1_out9), .out10(decoder_1_out10), .out11(decoder_1_out11),
    .out12(decoder_1_out12), .out13(decoder_1_out13), .out14(decoder_1_out14), .out15(decoder_1_out15),
    .sel(RegSel));
  and and_1 (and_1_out, decoder_1_out0, WrReg);
  and and_2 (and_2_out, decoder_1_out1, WrReg);
  and and_3 (and_3_out, decoder_1_out2, WrReg);
  and and_4 (and_4_out, decoder_1_out3, WrReg);
  and and_5 (and_5_out, decoder_1_out4, WrReg);
  and and_6 (and_6_out, decoder_1_out5, WrReg);
  and and_7 (and_7_out, decoder_1_out6, WrReg);
  and and_8 (and_8_out, decoder_1_out7, WrReg);
  and and_9 (and_9_out, decoder_1_out8, WrReg);
  and and_10 (and_10_out, decoder_1_out9, WrReg);
  and and_11 (and_11_out, decoder_1_out10, WrReg);
  and and_12 (and_12_out, decoder_1_out11, WrReg);
  and and_13 (and_13_out, decoder_1_out12, WrReg);
  and and_14 (and_14_out, decoder_1_out13, WrReg);
  and and_15 (and_15_out, decoder_1_out14, WrReg);
  and and_16 (and_16_out, decoder_1_out15, WrReg);
  Register #(.width(32)) u_zero (.D(Data_In), .en(and_1_out), .Q(zero), .clk(Clock), .clr(1'b1));
  Register #(.width(32)) u_at (.D(Data_In), .en(and_2_out), .Q(at), .clk(Clock), .clr(ClearRegFile));
  Register #(.width(32)) u_v0 (.D(Data_In), .en(and_3_out), .Q(v0), .clk(Clock), .clr(ClearRegFile));
  Register #(.width(32)) u_a0 (.D(Data_In), .en(and_4_out), .Q(a0), .clk(Clock), .clr(ClearRegFile));
  Register #(.width(32)) u_a1 (.D(Data_In), .en(and_5_out), .Q(a1), .clk(Clock), .clr(ClearRegFile));
  Register #(.width(32)) u_a2 (.D(Data_In), .en(and_6_out), .Q(a2), .clk(Clock), .clr(ClearRegFile));
  Register #(.width(32)) u_t0 (.D(Data_In), .en(and_7_out), .Q(t0), .clk(Clock), .clr(ClearRegFile));
  Register #(.width(32)) u_t1 (.D(Data_In), .en(and_8_out), .Q(t1), .clk(Clock), .clr(ClearRegFile));
  Register #(.width(32)) u_t2 (.D(Data_In), .en(and_9_out), .Q(t2), .clk(Clock), .clr(ClearRegFile));
  Register #(.width(32)) u_s0 (.D(Data_In), .en(and_10_out), .Q(s0), .clk(Clock), .clr(ClearRegFile));
  Register #(.width(32)) u_s1 (.D(Data_In), .en(and_11_out), .Q(s1), .clk(Clock), .clr(ClearRegFile));
  Register #(.width(32)) u_s2 (.D(Data_In), .en(and_12_out), .Q(s2), .clk(Clock), .clr(ClearRegFile));
  Register #(.width(32)) u_k0 (.D(Data_In), .en(and_13_out), .Q(k0), .clk(Clock), .clr(ClearRegFile));
  Register #(.width(32)) u_sp (.D(Data_In), .en(and_14_out), .Q(sp), .clk(Clock), .clr(ClearRegFile));
  Register #(.width(32)) u_pr (.D(Data_In), .en(and_15_out), .Q(pr), .clk(Clock), .clr(ClearRegFile));
  Register #(.width(32)) u_ra (.D(Data_In), .en(and_16_out), .Q(ra), .clk(Clock), .clr(ClearRegFile));
  Multiplexer #(.select(4), .width(32), .enable("false")) multiplexer_1 (
    .in0(zero), .in1(at), .in2(v0), .in3(a0), .in4(a1), .in5(a2), .in6(t0), .in7(t1), .in8(t2), .in9(s0),
    .in10(s1), .in11(s2), .in12(k0), .in13(sp), .in14(pr), .in15(ra), .out(Data_Out), .sel(RegSel));

  // Other names for the same wires on the sheet: Din[31:0] = Data_In; en = WrReg
endmodule

module Intergenerator (
  input  CLK,
  output [10:0] out_2,
  output IntOut
);

  wire button_1_out, register_2_q;
  wire [10:0] adder_1_out;

  Adder #(.width(11)) adder_1 (.a(11'h1), .b(out_2), .out(adder_1_out));  // open: cin, cout
  Register #(.width(11)) register_1 (.D(adder_1_out), .en(1'b1), .Q(out_2), .clk(CLK), .clr(register_2_q));
  Button button_1 (.out(button_1_out));
  Comparator #(.width(11), .mode("unsigned")) comparator_1 (.a(11'h200), .b(out_2), .eq(IntOut));  // open: gt, lt
  Register #(.width(1)) register_2 (.D(IntOut), .en(1'b1), .Q(register_2_q), .clk(CLK), .clr(register_2_q));
endmodule
