// Logisim project p3.circ as structural Verilog: 11 circuits, main circuit main
module main (
  input  in_1,
  input  [31:0] Constant_4,
  output [31:0] out_3,
  output [1:0] out_4,
  output [1:0] out_5
);

  wire alusrc, and_1_out, button_1_out, Clk, comparator_1_eq, control_1_rz_or_rx, dected_if_id_write,
       dected_pcwrite, dected_stall, EX_MEM_brance_or_not, IF_IDRR_beq, or_1_out, or_2_out;
  wire [1:0] control_1_out_4, EX_MEM_memtoreg_regwrite, func, ID_EX_memtoreg_regwrite,
       MEM_WB_memtoreg_regwrite;
  wire [2:0] EX_MEM_branch_memread_memwrite, ID_EX_branch_memread_memwrite;
  wire [3:0] EX_MEM_rx, ID_EX_rx, ID_EX_ry, ID_EX_rz, IF_IDRR_opcode, IF_IDRR_rx, IF_IDRR_ry, IF_IDRR_rz,
       MEM_WB_write_register_2;
  wire [8:0] multiplexer_3_out;
  wire [8:2] control_1_out_2;
  wire [19:0] IF_IDRR_offset;
  wire [31:0] adder_1_out, adder_2_out, dual_ported_register_file_1_out1, dual_ported_register_file_1_out2,
       EX_MEM_result_2, EX_MEM_result_3, EX_MEM_rz_2, ID_EX_data1, ID_EX_data2, ID_EX_pc, ID_EX_signextend,
       IF_IDRR_pc_2, MEM_WB_addres_2, MEM_WB_read_data_2, multiplexer_1_out, multiplexer_2_out,
       multiplexer_4_out, multiplexer_5_out, multiplexer_6_out, multiplexer_7_out, PC_q, ram_1_data,
       ram_2_data, SE_out_2;

  Clock clock_1 (.out(Clk));
  Multiplexer #(.width(32), .enable("false")) multiplexer_1 (
    .in0(adder_1_out), .in1(EX_MEM_result_2), .out(multiplexer_1_out), .sel(and_1_out));
  Multiplexer #(.width(32), .enable("false")) multiplexer_2 (
    .in0(PC_q), .in1(multiplexer_1_out), .out(multiplexer_2_out), .sel(dected_pcwrite));
  Register #(.width(32)) PC (.D(multiplexer_2_out), .en(1'b1), .Q(PC_q), .clk(Clk), .clr(in_1));
  dected_unit dected (
    .ID_EX_MemRead(ID_EX_branch_memread_memwrite[1]), .ID_EX_RegisterRx(ID_EX_rx),
    .IF_ID_RegisterRy(IF_IDRR_ry), .IF_ID_RegisterRz(IF_IDRR_rz), .Stall(dected_stall),
    .PCWrite(dected_pcwrite), .IF_ID_Write(dected_if_id_write));
  Adder #(.width(32)) adder_1 (.a(32'h1), .b(PC_q), .out(adder_1_out));  // open: cin, cout
  Button button_1 (.out(button_1_out));
  RAM #(.addrWidth(24), .dataWidth(32)) ram_1 (
    .addr(PC_q[23:0]), .data(ram_1_data), .clr(button_1_out));  // open: sel, clk, ld
  or or_1 (or_1_out, and_1_out, and_1_out, in_1);
  control control_1 (
    .in_1(IF_IDRR_opcode), .out_4(control_1_out_4), .out_2(control_1_out_2[2]), .Branch(control_1_out_2[5]),
    .MemToReg(control_1_out_2[6]), .MemRead(control_1_out_2[4]), .MemWrite(control_1_out_2[3]),
    .RegWrite(control_1_out_2[7]), .rz_or_rx(control_1_rz_or_rx));
  IF_IDRR_Buffer IF_IDRR (
    .opcode(IF_IDRR_opcode), .rx(IF_IDRR_rx), .ry(IF_IDRR_ry), .instuction(ram_1_data), .rz(IF_IDRR_rz),
    .offset(IF_IDRR_offset), .in_1(Clk), .Clear(or_1_out), .pc(adder_1_out), .pc_2(IF_IDRR_pc_2),
    .IF_ID_Write(dected_if_id_write), .in_5(control_1_rz_or_rx), .beq(IF_IDRR_beq));
  Multiplexer #(.width(9), .enable("false")) multiplexer_3 (
    .in0({control_1_out_2, control_1_out_4}), .in1({9{1'b0}}), .out(multiplexer_3_out), .sel(dected_stall));
  SE SE (.in_1(IF_IDRR_offset), .out_2(SE_out_2));
  Dual_Ported_Register_File dual_ported_register_file_1 (
    .CLK(Clk), .WrEN(MEM_WB_memtoreg_regwrite[0]), .OUT1(dual_ported_register_file_1_out1),
    .WrREGNO(MEM_WB_write_register_2), .RdREGNO1(IF_IDRR_ry), .RdREGNO2(IF_IDRR_rz),
    .OUT2(dual_ported_register_file_1_out2), .INPUT(multiplexer_7_out));
  or or_2 (or_2_out, and_1_out, in_1);
  IDRR_EX_Buffer ID_EX (
    .Clock(Clk), .Clear(or_2_out), .in_3({multiplexer_3_out[6], multiplexer_3_out[7]}),
    .MemToReg_RegWrite(ID_EX_memtoreg_regwrite), .in_4(multiplexer_3_out[5:3]),
    .Branch_MemRead_MemWrite(ID_EX_branch_memread_memwrite), .in_5(multiplexer_3_out[2:0]),
    .AluOP1_ALUOP0_AluSrc({alusrc, func}), .in_6(IF_IDRR_pc_2), .PC(ID_EX_pc),
    .in_7(dual_ported_register_file_1_out1), .Data1(ID_EX_data1), .in_8(dual_ported_register_file_1_out2),
    .Data2(ID_EX_data2), .in_9(SE_out_2), .SignExtend(ID_EX_signextend), .in_10(IF_IDRR_rx), .Rx(ID_EX_rx),
    .in_11(IF_IDRR_ry), .Ry(ID_EX_ry), .in_12(IF_IDRR_rz), .Rz(ID_EX_rz));
  Adder #(.width(32)) adder_2 (.a(ID_EX_pc), .b(ID_EX_signextend), .out(adder_2_out));  // open: cin, cout
  Multiplexer #(.select(2), .width(32), .enable("false")) multiplexer_4 (
    .in0(ID_EX_data2), .in1(multiplexer_7_out), .in2(EX_MEM_result_3), .out(multiplexer_4_out), .sel(out_5));  // open: in3
  Multiplexer #(.select(2), .width(32), .enable("false")) multiplexer_5 (
    .in0(ID_EX_data1), .in1(multiplexer_7_out), .in2(EX_MEM_result_3), .out(multiplexer_5_out), .sel(out_4));  // open: in3
  Multiplexer #(.width(32), .enable("false")) multiplexer_6 (
    .in0(multiplexer_4_out), .in1(ID_EX_signextend), .out(multiplexer_6_out), .sel(alusrc));
  ALU alu_1 (.FUNC(func), .A(multiplexer_5_out), .B(multiplexer_6_out), .OUT(out_3));
  forward forward (
    .EX_MEM_RegWrite(EX_MEM_memtoreg_regwrite[0]), .EX_MEM_RegisterRx(EX_MEM_rx),
    .ID_EX_RegisterRy(ID_EX_ry), .ID_EX_RegisterRz(ID_EX_rz), .MEM_WB_RegisterRx(MEM_WB_write_register_2),
    .MEM_WB_RegWrite(MEM_WB_memtoreg_regwrite[1]), .ForwardA(out_4), .ForwardB(out_5));
  Comparator #(.width(32)) comparator_1 (.a(out_3), .b({32{1'b0}}), .eq(comparator_1_eq));  // open: gt, lt
  EX_MEM_Buffer EX_MEM (
    .Clock(Clk), .Clear(in_1), .in_3(ID_EX_memtoreg_regwrite), .in_4(ID_EX_branch_memread_memwrite),
    .Result(out_3), .in_7(comparator_1_eq), .in_8(ID_EX_rx), .MemToReg_RegWrite(EX_MEM_memtoreg_regwrite),
    .Branch_MemRead_MemWrite(EX_MEM_branch_memread_memwrite), .Result_3(EX_MEM_result_3),
    .brance_or_not(EX_MEM_brance_or_not), .Rx(EX_MEM_rx), .rz(multiplexer_4_out), .rz_2(EX_MEM_rz_2),
    .add(adder_2_out), .Result_2(EX_MEM_result_2));
  and and_1 (and_1_out, EX_MEM_branch_memread_memwrite[2], EX_MEM_brance_or_not);
  RAM #(.addrWidth(24), .dataWidth(32), .bus("separate")) ram_2 (
    .addr(EX_MEM_result_3[23:0]), .din(EX_MEM_rz_2), .data(ram_2_data),
    .str(EX_MEM_branch_memread_memwrite[0]), .clk(Clk), .ld(EX_MEM_branch_memread_memwrite[1]), .clr(in_1));  // open: sel
  MEM_WB_Buffer MEM_WB (
    .Clock(Clk), .Clear(in_1), .in_3(EX_MEM_memtoreg_regwrite), .Read_data(ram_2_data),
    .Addres(EX_MEM_result_3), .write_register(EX_MEM_rx), .MemToReg_RegWrite(MEM_WB_memtoreg_regwrite),
    .Read_data_2(MEM_WB_read_data_2), .Addres_2(MEM_WB_addres_2), .write_register_2(MEM_WB_write_register_2));  // open: PC, PC_2
  Multiplexer #(.width(32), .enable("false")) multiplexer_7 (
    .in0(MEM_WB_addres_2), .in1(MEM_WB_read_data_2), .out(multiplexer_7_out),
    .sel(MEM_WB_memtoreg_regwrite[1]));

  // Other names for the same wires on the sheet: Clear = in_1
endmodule

module Dual_Ported_Register_File (
  input  CLK,
  input  WrEN,
  input  [3:0] WrREGNO,
  input  [3:0] RdREGNO1,
  input  [3:0] RdREGNO2,
  input  [31:0] INPUT,
  output [31:0] OUT1,
  output [31:0] OUT2
);

  wire button_1_out, En_a0, En_a1, En_a2, En_a3, En_a4, En_at, En_fp, En_k0, En_ra, En_s0, En_s1, En_s2,
       En_s3, En_sp, En_v0;
  wire [31:0] a0, a1, a2, a3, a4, at, fp, k0, ra, s0, s1, s2, s3, sp, v0, zero;

  Decoder #(.select(4), .disabled(0)) decoder_1 (
    .out1(En_at), .out2(En_v0), .out3(En_a0), .out4(En_a1), .out5(En_a2), .out6(En_a3), .out7(En_a4),
    .out8(En_s0), .out9(En_s1), .out10(En_s2), .out11(En_s3), .out12(En_k0), .out13(En_sp), .out14(En_fp),
    .out15(En_ra), .sel(WrREGNO), .en(WrEN));  // open: out0
  Register #(.width(32)) u_zero (.D(INPUT), .en(1'b0), .Q(zero), .clk(CLK));  // open: clr
  Register #(.width(32)) u_at (.D(INPUT), .en(En_at), .Q(at), .clk(CLK));  // open: clr
  Register #(.width(32)) u_v0 (.D(INPUT), .en(En_v0), .Q(v0), .clk(CLK));  // open: clr
  Register #(.width(32)) u_a0 (.D(INPUT), .en(En_a0), .Q(a0), .clk(CLK), .clr(button_1_out));
  Register #(.width(32)) u_a1 (.D(INPUT), .en(En_a1), .Q(a1), .clk(CLK));  // open: clr
  Register #(.width(32)) u_a2 (.D(INPUT), .en(En_a2), .Q(a2), .clk(CLK));  // open: clr
  Register #(.width(32)) u_a3 (.D(INPUT), .en(En_a3), .Q(a3), .clk(CLK));  // open: clr
  Register #(.width(32)) u_a4 (.D(INPUT), .en(En_a4), .Q(a4), .clk(CLK));  // open: clr
  Multiplexer #(.select(4), .width(32), .disabled(0), .enable("false")) multiplexer_1 (
    .in0(zero), .in1(at), .in2(v0), .in3(a0), .in4(a1), .in5(a2), .in6(a3), .in7(a4), .in8(s0), .in9(s1),
    .in10(s2), .in11(s3), .in12(k0), .in13(sp), .in14(fp), .in15(ra), .out(OUT2), .sel(RdREGNO2));
  Register #(.width(32)) u_s0 (.D(INPUT), .en(En_s0), .Q(s0), .clk(CLK), .clr(button_1_out));
  Register #(.width(32)) u_s1 (.D(INPUT), .en(En_s1), .Q(s1), .clk(CLK), .clr(button_1_out));
  Register #(.width(32)) u_s2 (.D(INPUT), .en(En_s2), .Q(s2), .clk(CLK), .clr(button_1_out));
  Register #(.width(32)) u_s3 (.D(INPUT), .en(En_s3), .Q(s3), .clk(CLK), .clr(button_1_out));
  Button button_1 (.out(button_1_out));
  Register #(.width(32)) u_k0 (.D(INPUT), .en(En_k0), .Q(k0), .clk(CLK));  // open: clr
  Register #(.width(32)) u_sp (.D(INPUT), .en(En_sp), .Q(sp), .clk(CLK));  // open: clr
  Register #(.width(32)) u_fp (.D(INPUT), .en(En_fp), .Q(fp), .clk(CLK));  // open: clr
  Register #(.width(32)) u_ra (.D(INPUT), .en(En_ra), .Q(ra), .clk(CLK));  // open: clr
  Multiplexer #(.select(4), .width(32), .disabled(0), .enable("false")) multiplexer_2 (
    .in0(zero), .in1(at), .in2(v0), .in3(a0), .in4(a1), .in5(a2), .in6(a3), .in7(a4), .in8(s0), .in9(s1),
    .in10(s2), .in11(s3), .in12(k0), .in13(sp), .in14(fp), .in15(ra), .out(OUT1), .sel(RdREGNO1));

  // Notes on the sheet:
  //   DO NOT MODIFY THIS FILE
endmodule

module IF_IDRR_Buffer (
  input  in_1,
  input  Clear,
  input  IF_ID_Write,
  input  [31:0] instuction,
  input  in_5,
  input  [31:0] pc,
  output [3:0] opcode,
  output [3:0] rx,
  output [3:0] ry,
  output [3:0] rz,
  output [19:0] offset,
  output beq,
  output [31:0] pc_2
);

  Register #(.width(32)) register_1 (
    .D(instuction), .en(IF_ID_Write), .Q({opcode, rx, ry, offset}), .clk(in_1), .clr(Clear));
  Register #(.width(32)) register_2 (.D(pc), .en(IF_ID_Write), .Q(pc_2), .clk(in_1), .clr(Clear));
  Comparator #(.width(4)) comparator_1 (.a(opcode), .b(4'b0101), .eq(beq));  // open: gt, lt
  Multiplexer #(.width(4), .enable("false")) multiplexer_1 (.in0(offset[3:0]), .in1(rx), .out(rz), .sel(in_5));

  // Other names for the same wires on the sheet: Clk = in_1
endmodule

module IDRR_EX_Buffer (
  input  Clock,
  input  Clear,
  input  [1:0] in_3,
  input  [2:0] in_4,
  input  [2:0] in_5,
  input  [31:0] in_6,
  input  [31:0] in_7,
  input  [31:0] in_8,
  input  [31:0] in_9,
  input  [3:0] in_10,
  input  [3:0] in_11,
  input  [3:0] in_12,
  output [1:0] MemToReg_RegWrite,
  output [2:0] Branch_MemRead_MemWrite,
  output [2:0] AluOP1_ALUOP0_AluSrc,
  output [31:0] PC,
  output [31:0] Data1,
  output [31:0] Data2,
  output [31:0] SignExtend,
  output [3:0] Rx,
  output [3:0] Ry,
  output [3:0] Rz
);

  Register #(.width(2)) WB (.D(in_3), .en(1'b1), .Q(MemToReg_RegWrite), .clk(Clock), .clr(Clear));
  Register #(.width(3)) M (.D(in_4), .en(1'b1), .Q(Branch_MemRead_MemWrite), .clk(Clock), .clr(Clear));
  Register #(.width(3)) EX (.D(in_5), .en(1'b1), .Q(AluOP1_ALUOP0_AluSrc), .clk(Clock), .clr(Clear));
  Register #(.width(32)) register_1 (.D(in_6), .en(1'b1), .Q(PC), .clk(Clock));  // open: clr
  Register #(.width(32)) register_2 (.D(in_7), .en(1'b1), .Q(Data1), .clk(Clock), .clr(Clear));
  Register #(.width(32)) register_3 (.D(in_8), .en(1'b1), .Q(Data2), .clk(Clock), .clr(Clear));
  Register #(.width(32)) register_4 (.D(in_9), .en(1'b1), .Q(SignExtend), .clk(Clock), .clr(Clear));
  Register #(.width(4)) register_5 (.D(in_10), .en(1'b1), .Q(Rx), .clk(Clock), .clr(Clear));
  Register #(.width(4)) register_6 (.D(in_11), .en(1'b1), .Q(Ry), .clk(Clock), .clr(Clear));
  Register #(.width(4)) register_7 (.D(in_12), .en(1'b1), .Q(Rz), .clk(Clock), .clr(Clear));
endmodule

module EX_MEM_Buffer (
  input  Clock,
  input  Clear,
  input  [1:0] in_3,
  input  [2:0] in_4,
  input  [31:0] add,
  input  [31:0] Result,
  input  in_7,
  input  [3:0] in_8,
  input  [31:0] rz,
  output [1:0] MemToReg_RegWrite,
  output [2:0] Branch_MemRead_MemWrite,
  output [31:0] Result_2,
  output [31:0] Result_3,
  output brance_or_not,
  output [3:0] Rx,
  output [31:0] rz_2
);

  Register #(.width(2)) WB (.D(in_3), .en(1'b1), .Q(MemToReg_RegWrite), .clk(Clock), .clr(Clear));
  Register #(.width(3)) M (.D(in_4), .en(1'b1), .Q(Branch_MemRead_MemWrite), .clk(Clock), .clr(Clear));
  Register #(.width(32)) register_1 (.D(add), .en(1'b1), .Q(Result_2), .clk(Clock), .clr(Clear));
  Register #(.width(32)) register_2 (.D(Result), .en(1'b1), .Q(Result_3), .clk(Clock), .clr(Clear));
  Register #(.width(1)) branch (.D(in_7), .en(1'b1), .Q(brance_or_not), .clk(Clock), .clr(Clear));
  Register #(.width(4)) register_3 (.D(in_8), .en(1'b1), .Q(Rx), .clk(Clock), .clr(Clear));
  Register #(.width(32)) register_4 (.D(rz), .en(1'b1), .Q(rz_2), .clk(Clock), .clr(Clear));
endmodule

module MEM_WB_Buffer (
  input  Clock,
  input  Clear,
  input  [1:0] in_3,
  input  [31:0] Read_data,
  input  [31:0] Addres,
  input  [3:0] write_register,
  input  [31:0] PC,
  output [1:0] MemToReg_RegWrite,
  output [31:0] Read_data_2,
  output [31:0] Addres_2,
  output [3:0] write_register_2,
  output [31:0] PC_2
);

  Register #(.width(2)) register_1 (.D(in_3), .en(1'b1), .Q(MemToReg_RegWrite), .clk(Clock), .clr(Clear));
  Register #(.width(32)) register_2 (.D(Read_data), .en(1'b1), .Q(Read_data_2), .clk(Clock), .clr(Clear));
  Register #(.width(32)) register_3 (.D(Addres), .en(1'b1), .Q(Addres_2), .clk(Clock), .clr(Clear));
  Register #(.width(4)) register_4 (.D(write_register), .en(1'b1), .Q(write_register_2), .clk(Clock), .clr(Clear));
  Register #(.width(32)) register_5 (.D(PC), .en(1'b1), .Q(PC_2), .clk(Clock), .clr(Clear));
endmodule

module ALU (
  input  [1:0] FUNC,
  input  [31:0] A,
  input  [31:0] B,
  output [31:0] OUT
);

  wire [31:0] adder_1_out, adder_2_out, nand_1_out, subtractor_1_out;

  Adder #(.width(32)) adder_1 (.a(A), .b(B), .out(adder_1_out), .cin(1'b0));  // open: cout
  assign nand_1_out = ~(A & B);  // NAND_Gate nand_1, 32 bits wide
  Subtractor #(.width(32)) subtractor_1 (.a(A), .b(B), .out(subtractor_1_out), .bin(1'b0));  // open: bout
  Adder #(.width(32)) adder_2 (.a(A), .b(B), .out(adder_2_out), .cin(1'b1));  // open: cout
  Multiplexer #(.select(2), .width(32), .disabled(0), .enable("false")) multiplexer_1 (
    .in0(adder_1_out), .in1(nand_1_out), .in2(subtractor_1_out), .in3(adder_2_out), .out(OUT), .sel(FUNC));

  // Notes on the sheet:
  //   DO NOT MODIFY THIS
endmodule

module SE (
  input  [19:0] in_1,
  output [31:0] out_2
);


  assign out_2 = {{13{in_1[19]}}, in_1[18:0]};
endmodule

module control (
  input  [3:0] in_1,
  output out_2,
  output Branch,
  output [1:0] out_4,
  output MemRead,
  output MemToReg,
  output MemWrite,
  output RegWrite,
  output rz_or_rx
);

  Multiplexer #(.select(4), .enable("false")) multiplexer_1 (
    .in0(1'b0), .in1(1'b0), .in2(1'b0), .in3(1'b0), .in4(1'b1), .in5(1'b1), .out(rz_or_rx), .sel(in_1));  // open: in6, in7, in8, in9, in10, in11, in12, in13, in14, in15
  Multiplexer #(.select(4), .width(2), .enable("false")) multiplexer_2 (
    .in0(2'b00), .in1(2'b01), .in2(2'b00), .in3(2'b00), .in4(2'b00), .in5(2'b10), .out(out_4), .sel(in_1));  // open: in6, in7, in8, in9, in10, in11, in12, in13, in14, in15
  Multiplexer #(.select(4), .enable("false")) multiplexer_3 (
    .in0(1'b0), .in1(1'b0), .in2(1'b1), .in3(1'b1), .in4(1'b1), .in5(1'b0), .out(out_2), .sel(in_1));  // open: in6, in7, in8, in9, in10, in11, in12, in13, in14, in15
  Multiplexer #(.select(4), .enable("false")) multiplexer_4 (
    .in0(1'b0), .in1(1'b0), .in2(1'b0), .in3(1'b0), .in4(1'b0), .in5(1'b1), .out(Branch), .sel(in_1));  // open: in6, in7, in8, in9, in10, in11, in12, in13, in14, in15
  Multiplexer #(.select(4), .enable("false")) multiplexer_5 (
    .in0(1'b0), .in1(1'b0), .in2(1'b0), .in3(1'b1), .in4(1'b0), .in5(1'b0), .out(MemToReg), .sel(in_1));  // open: in6, in7, in8, in9, in10, in11, in12, in13, in14, in15
  Multiplexer #(.select(4), .enable("false")) multiplexer_6 (
    .in0(1'b1), .in1(1'b1), .in2(1'b1), .in3(1'b1), .in4(1'b0), .in5(1'b0), .out(RegWrite), .sel(in_1));  // open: in6, in7, in8, in9, in10, in11, in12, in13, in14, in15
  Multiplexer #(.select(4), .enable("false")) multiplexer_7 (
    .in0(1'b0), .in1(1'b0), .in2(1'b0), .in3(1'b1), .in4(1'b0), .in5(1'b0), .out(MemRead), .sel(in_1));  // open: in6, in7, in8, in9, in10, in11, in12, in13, in14, in15
  Multiplexer #(.select(4), .enable("false")) multiplexer_8 (
    .in0(1'b0), .in1(1'b0), .in2(1'b0), .in3(1'b0), .in4(1'b1), .in5(1'b0), .out(MemWrite), .sel(in_1));  // open: in6, in7, in8, in9, in10, in11, in12, in13, in14, in15

  // Other names for the same wires on the sheet: ALUsrc = out_2; func[1:0] = out_4
endmodule

module forward (
  input  EX_MEM_RegWrite,
  input  [3:0] EX_MEM_RegisterRx,
  input  [3:0] ID_EX_RegisterRy,
  input  [3:0] ID_EX_RegisterRz,
  input  [3:0] MEM_WB_RegisterRx,
  input  MEM_WB_RegWrite,
  output [1:0] ForwardA,
  output [1:0] ForwardB
);

  wire comparator_1_eq, comparator_2_eq, comparator_3_eq, comparator_4_eq, comparator_5_eq, comparator_6_eq,
       not_1_out, not_2_out, not_3_out, not_4_out;

  Comparator #(.width(4)) comparator_1 (.a(EX_MEM_RegisterRx), .b(4'b0000), .eq(comparator_1_eq));  // open: gt, lt
  Comparator #(.width(4)) comparator_2 (
    .a(EX_MEM_RegisterRx), .b(ID_EX_RegisterRy), .eq(comparator_2_eq));  // open: gt, lt
  Comparator #(.width(4)) comparator_3 (
    .a(EX_MEM_RegisterRx), .b(ID_EX_RegisterRz), .eq(comparator_3_eq));  // open: gt, lt
  Comparator #(.width(4)) comparator_4 (.a(MEM_WB_RegisterRx), .b(4'b0000), .eq(comparator_4_eq));  // open: gt, lt
  Comparator #(.width(4)) comparator_5 (
    .a(ID_EX_RegisterRy), .b(MEM_WB_RegisterRx), .eq(comparator_5_eq));  // open: gt, lt
  Comparator #(.width(4)) comparator_6 (
    .a(MEM_WB_RegisterRx), .b(ID_EX_RegisterRz), .eq(comparator_6_eq));  // open: gt, lt
  not not_1 (not_1_out, comparator_1_eq);
  not not_2 (not_2_out, comparator_4_eq);
  and and_1 (ForwardA[1], EX_MEM_RegWrite, not_1_out, comparator_2_eq);
  not not_3 (not_3_out, comparator_2_eq);
  not not_4 (not_4_out, comparator_3_eq);
  and and_2 (ForwardB[1], not_1_out, EX_MEM_RegWrite, comparator_3_eq);
  and and_3 (ForwardA[0], not_4_out, not_2_out, comparator_5_eq, MEM_WB_RegWrite);
  and and_4 (ForwardB[0], not_3_out, MEM_WB_RegWrite, not_2_out, comparator_6_eq);

  // Notes on the sheet:
  //   A=10
  //   A=01
  //   B=10
  //   b=01
endmodule

module dected_unit (
  input  ID_EX_MemRead,
  input  [3:0] ID_EX_RegisterRx,
  input  [3:0] IF_ID_RegisterRy,
  input  [3:0] IF_ID_RegisterRz,
  output Stall,
  output PCWrite,
  output IF_ID_Write
);

  wire comparator_1_eq, comparator_2_eq, or_1_out;

  Comparator #(.width(4)) comparator_1 (
    .a(ID_EX_RegisterRx), .b(IF_ID_RegisterRy), .eq(comparator_1_eq));  // open: gt, lt
  Comparator #(.width(4)) comparator_2 (
    .a(ID_EX_RegisterRx), .b(IF_ID_RegisterRz), .eq(comparator_2_eq));  // open: gt, lt
  and and_1 (Stall, ID_EX_MemRead, or_1_out);
  not not_1 (IF_ID_Write, Stall);
  or or_1 (or_1_out, comparator_1_eq, comparator_2_eq);

  assign PCWrite = IF_ID_Write;
endmodule
